# Fritzing sketch NKE_Boitier-5 (saved by Fritzing 0.9.2b)
circuit board: 9.9296cm x 2.45869cm
breadboards: 1

parts:
  Bus = screw terminal, 3 pins
  Aff1 = screw terminal, 3 pins
  Loch = screw terminal, 3 pins
  Aerien = screw terminal, 3 pins
  Bus_2 = screw terminal, 3 pins

nets:
  N1: Bus.pin1, Aff1.pin1, Loch.pin1, Aerien.pin1, Bus_2.pin1
  N2: Bus.pin2, Aff1.pin2, Loch.pin2, Aerien.pin2, Bus_2.pin2
  N3: Bus.pin3, Aff1.pin3, Loch.pin3, Aerien.pin3, Bus_2.pin3
