# Fritzing sketch NKE_Boitier-5_Alim_Cascade_NMEA-2 (saved by Fritzing 0.9.2b)
circuit board: 9.91088cm x 4.45291cm
breadboards: 1

parts:
  Aerien = screw terminal, 3 pins
  Loch = screw terminal, 3 pins
  Aff1 = screw terminal, 3 pins
  Compas = screw terminal, 3 pins
  Pilote = screw terminal, 3 pins

nets:
  N1: Aerien.pin1, Loch.pin1, Aff1.pin1, Compas.pin1, Pilote.pin1
  N2: Aerien.pin2, Loch.pin2, Aff1.pin2, Compas.pin2, Pilote.pin2
  N3: Aerien.pin3, Loch.pin3, Aff1.pin3, Compas.pin3, Pilote.pin3
