# Fritzing sketch NKE_Boitier-7_NMEA-2 (saved by Fritzing 0.9.2b)
circuit board: 9.76378cm x 4.41613cm
breadboards: 1

parts:
  Aerien = screw terminal, 3 pins
  Loch = screw terminal, 3 pins
  Aff1 = screw terminal, 3 pins
  Compas = screw terminal, 3 pins
  Pilote = screw terminal, 3 pins
  Bus = screw terminal, 3 pins
  Alim = screw terminal, 3 pins
  NMEA_2 = screw terminal, 3 pins
  NMEA_1 = screw terminal, 3 pins

nets:
  N1: Aerien.pin1, Loch.pin1, Aff1.pin1, Compas.pin1, Pilote.pin1, Bus.pin1, Alim.pin1
  N2: Aerien.pin2, Loch.pin2, Aff1.pin2, Compas.pin2, Pilote.pin2, Bus.pin2, Alim.pin2
  N3: Aerien.pin3, Loch.pin3, Aff1.pin3, Compas.pin3, Pilote.pin3, Bus.pin3, Alim.pin3
  N4: NMEA_2.pin1, NMEA_1.pin3
  N5: NMEA_2.pin2, NMEA_1.pin2
  N6: NMEA_2.pin3, NMEA_1.pin1
